// Digital circuit main.dig as structural Verilog
module main (
);

  wire ADDR_RS0_A, ADDR_RS0_B, ADDR_RS0_C, ADDR_RS0_D, ADDR_RS1_A, ADDR_RS1_B, ADDR_RS1_C, ADDR_RS1_D,
       ALU_A_IN_A, ALU_A_IN_B, ALU_B_IN_A, ALU_B_IN_B, ALU_C_IN_A, ALU_C_IN_B, ALU_D_IN_A, ALU_D_IN_B, imm8,
       imm16, instruction_decoder_1_p2, instruction_decoder_1_p3, instruction_decoder_1_p4,
       instruction_decoder_1_p9, instruction_decoder_1_p12, instruction_decoder_1_p17,
       instruction_decoder_1_p18, nand_1_out, ooo, PC_2_ovf, PC_ovf, undriven, undriven_2, undriven_3;
  wire [1:0] ll, rs1;
  wire [2:0] rs0, vvv;
  wire [3:0] alu_1_fl, Flag_q;
  wire [7:0] A_q, ACC_q, alu_1_out, B_q, C_q, D_q, driver_4_out, driver_16_out, driver_17_out,
       instruction_decoder_1_p8, instruction_decoder_1_p11, IR0_q, PC_2_hi, PC_2_lo, PC_hi, PC_lo;
  wire [15:0] driver_1_out, driver_6_out;

  _16_bit_presettable_counter PC (
    .dir(1'b0), .lo_in(driver_4_out), .lo_ld(1'b0), .hi_in(driver_4_out), .hi_ld(1'b0), .clr(1'b0),
    .ovf(PC_ovf), .lo(PC_lo), .hi(PC_hi));  // open: en, c
  _16_bit_presettable_counter PC_2 (
    .en(1'b1), .dir(1'b0), .lo_in(driver_4_out), .lo_ld(1'b0), .hi_in(driver_4_out), .hi_ld(1'b0),
    .clr(1'b0), .ovf(PC_2_ovf), .lo(PC_2_lo), .hi(PC_2_hi));  // open: c
  LED led_1 (.in(PC_ovf));
  Driver #(.Bits(16)) driver_1 (.in({PC_hi, PC_lo}), .out(driver_1_out));  // open: en
  LED led_2 (.in(PC_2_ovf));
  Driver #(.Bits(16)) driver_2 (.in({PC_2_hi, PC_2_lo}), .out(driver_1_out));  // open: en
  Driver driver_3 (.in(driver_6_out[0]), .out(driver_1_out[0]));  // open: en
  Register #(.Bits(8)) IR0 (.D(driver_4_out), .C(instruction_decoder_1_p2), .en(instruction_decoder_1_p3), .Q(IR0_q));
  Register #(.Bits(8)) A (.D(driver_4_out), .Q(A_q));  // open: C, en
  Register #(.Bits(8)) B (.D(driver_4_out), .Q(B_q));  // open: C, en
  Register #(.Bits(8)) C (.D(driver_4_out), .Q(C_q));  // open: C, en
  Register #(.Bits(8)) D (.D(driver_4_out), .Q(D_q));  // open: C, en
  assign driver_4_out = undriven_3 ? A_q : 8'bz;  // Driver driver_4
  assign driver_6_out[7:0] = ADDR_RS1_A ? A_q : 8'bz;  // Driver driver_5
  assign driver_6_out[15:8] = ADDR_RS0_A ? A_q : 8'bz;  // Driver driver_6
  assign driver_4_out = undriven_2 ? B_q : 8'bz;  // Driver driver_7
  assign driver_6_out[7:0] = ADDR_RS1_B ? B_q : 8'bz;  // Driver driver_8
  assign driver_6_out[15:8] = ADDR_RS0_B ? B_q : 8'bz;  // Driver driver_9
  assign driver_4_out = undriven ? C_q : 8'bz;  // Driver driver_10
  assign driver_6_out[7:0] = ADDR_RS1_C ? C_q : 8'bz;  // Driver driver_11
  assign driver_6_out[15:8] = ADDR_RS0_C ? C_q : 8'bz;  // Driver driver_12
  assign driver_4_out = instruction_decoder_1_p4 ? D_q : 8'bz;  // Driver driver_13
  assign driver_6_out[7:0] = ADDR_RS1_D ? D_q : 8'bz;  // Driver driver_14
  assign driver_6_out[15:8] = ADDR_RS0_D ? D_q : 8'bz;  // Driver driver_15
  // instruction_decoder instruction_decoder_1: pin names not known; wires that end beside it: driver_1_out, instruction_decoder_1_p2, instruction_decoder_1_p3, instruction_decoder_1_p4, ll, IR0_q, ooo, instruction_decoder_1_p8, instruction_decoder_1_p9, vvv, instruction_decoder_1_p11, instruction_decoder_1_p12, imm8, rs0, rs1, imm16, instruction_decoder_1_p17, instruction_decoder_1_p18
  Register #(.Bits(8)) IR1 (
    .D(driver_4_out), .C(instruction_decoder_1_p9), .en(instruction_decoder_1_p12),
    .Q(instruction_decoder_1_p8));
  assign driver_16_out = ALU_A_IN_B ? A_q : 8'bz;  // Driver driver_16
  assign driver_17_out = ALU_A_IN_A ? A_q : 8'bz;  // Driver driver_17
  assign driver_16_out = ALU_B_IN_B ? B_q : 8'bz;  // Driver driver_18
  assign driver_17_out = ALU_B_IN_A ? B_q : 8'bz;  // Driver driver_19
  assign driver_16_out = ALU_C_IN_B ? C_q : 8'bz;  // Driver driver_20
  assign driver_17_out = ALU_C_IN_A ? C_q : 8'bz;  // Driver driver_21
  assign driver_16_out = ALU_D_IN_B ? D_q : 8'bz;  // Driver driver_22
  assign driver_17_out = ALU_D_IN_A ? D_q : 8'bz;  // Driver driver_23
  Register #(.Bits(8)) IR2 (
    .D(driver_4_out), .C(instruction_decoder_1_p17), .en(instruction_decoder_1_p18),
    .Q(instruction_decoder_1_p11));
  Driver #(.Bits(8)) driver_24 (.in(alu_1_out), .out(driver_4_out));  // open: en
  Driver driver_25 (.in(imm8), .out(driver_16_out[0]));  // open: en
  alu alu_1 (.flags(Flag_q), .A(driver_17_out), .B(driver_16_out), .fl(alu_1_fl), .out(alu_1_out));  // open: op
  nand nand_1 (nand_1_out, ll[0], ll[1]);
  assign driver_17_out = nand_1_out ? ACC_q : 8'bz;  // Driver driver_26
  Driver #(.Bits(8)) driver_27 (.in(ACC_q), .out(driver_4_out));  // open: en
  Register #(.Bits(4)) Flag (.D(alu_1_fl), .Q(Flag_q));  // open: C, en
  Decoder #(.Selector_Bits(2)) decoder_1 (
    .sel(vvv[1:0]), .out_0(ALU_A_IN_B), .out_1(ALU_B_IN_B), .out_2(ALU_C_IN_B), .out_3(ALU_D_IN_B));
  Decoder #(.Selector_Bits(2)) decoder_2 (
    .sel(rs0[1:0]), .out_0(ALU_A_IN_A), .out_1(ALU_B_IN_A), .out_2(ALU_C_IN_A), .out_3(ALU_D_IN_A));
  Register #(.Bits(8)) ACC (.Q(ACC_q));  // open: D, C, en
  Decoder #(.Selector_Bits(2)) decoder_3 (
    .sel(rs0[1:0]), .out_0(ADDR_RS0_A), .out_1(ADDR_RS0_B), .out_2(ADDR_RS0_C), .out_3(ADDR_RS0_D));
  Decoder #(.Selector_Bits(2)) decoder_4 (
    .sel(rs1), .out_0(ADDR_RS1_A), .out_1(ADDR_RS1_B), .out_2(ADDR_RS1_C), .out_3(ADDR_RS1_D));
  // Pins of 1 and 8 bits meet at driver_16_out
  // Pins of 1 and 16 bits meet at driver_6_out
  // Pins of 1 and 16 bits meet at driver_1_out
  // Pins of 2 and 3 bits meet at rs0

  // Notes on the sheet:
  //   Program Counter
  //   Stack Pointer
  //   DBUS
  //   ABUS
  //   Registers
  //   Instruction Register
  //   Decoder
  //   ALU
  //   ALU BUS
  //   ALU Decoders
  //   ACC
  //   Flag register
  //   Address Decoders
endmodule
